# Fritzing sketch oscilator.Stepper (saved by Fritzing 0.9.3b)
stripboards: 1

parts:
  C1 = Electrolytic Capacitor [capacitance=1µF package="100 mil [THT, electrolytic]"]
  IC1 = IC, DIP package, 14 pins [chip_label=cd40106]
  R1 = Rotary Potentiometer (Small) [maximum_resistance=100kΩ package=THT]
  C2 = Electrolytic Capacitor [capacitance=1µF package="100 mil [THT, electrolytic]"]
  S1 = Toggle Switch [package=THT]
  Power_plug1 = Power plug
  R4 = Resistor [tolerance=±5% resistance=220 package=THT]
  LED1 = LED - 5mm [color="Red (633nm)" package="5 mm [THT]"]
  IC2 = IC, DIP package, 16 pins [chip_label=cd4040]
  IC3 = IC, DIP package, 16 pins [chip_label=cd4051]
  R3 = Resistor [tolerance=±5% resistance=220 package=THT]
  R9 = Resistor [tolerance=±5% resistance=220 package=THT]
  R10 = Resistor [tolerance=±5% resistance=220 package=THT]
  R12 = Resistor [tolerance=±5% resistance=220 package=THT]
  R13 = Resistor [tolerance=±5% resistance=220 package=THT]
  R14 = Resistor [tolerance=±5% resistance=220 package=THT]
  R15 = Resistor [tolerance=±5% resistance=220 package=THT]
  R16 = Resistor [tolerance=±5% resistance=220 package=THT]
  R17 = Resistor [tolerance=±5% resistance=220 package=THT]  # not connected

nets:
  N1: C1.-, IC1.pin7, R1.leg1, C2.-, S1.L1, LED1.cathode, IC2.pin8, IC3.pin6, IC3.pin7, IC3.pin8
  N2: C1.+, IC1.pin1, R1.leg2
  N3: IC1.pin2, R1.wiper, IC2.pin10
  N4: IC1.pin8, C2.+, IC3.pin3, R3.Pin_1
  N5: IC1.pin9, R3.Pin_0, R9.Pin_0, R10.Pin_0, R12.Pin_0, R13.Pin_0, R14.Pin_0, R15.Pin_0, R16.Pin_0
  N6: IC1.pin14, Power_plug1.VCC, R4.Pin_0, IC2.pin11, IC2.pin16, IC3.pin16
  N7: S1.COM, Power_plug1.GND
  N8: R4.Pin_1, LED1.anode
  N9: IC2.pin6, IC3.pin10
  N10: IC2.pin7, IC3.pin9
  N11: IC2.pin9, IC3.pin11
  N12: IC3.pin1, R13.Pin_1
  N13: IC3.pin2, R14.Pin_1
  N14: IC3.pin4, R15.Pin_1
  N15: IC3.pin5, R16.Pin_1
  N16: IC3.pin12, R12.Pin_1
  N17: IC3.pin14, R10.Pin_1
  N18: IC3.pin15, R9.Pin_1

notes:
  in design orient cd4016 perpendicular to other chips
  also, line the outputs on the 40106 with headers
  and have a switch for the multiplexer
  have a bank of capacitors for the oscilator
  out to amp
  power switch, input, & indicator
  LFO - clock
